// Logisim project NSU-FIT-2021-T04L1e01.circ as structural Verilog: 1 circuit, main circuit mycircuit
module mycircuit (
  input  A,
  input  B,
  input  C,
  output R
);

  or or_1 (R, A, C);
endmodule
