// Logisim project NSU-FIT-2021-T04L1e03_1.circ as structural Verilog: 1 circuit, main circuit mycircuit
module mycircuit (
  input  A,
  input  B,
  input  C,
  output R
);

  nor nor_1 (R, A, B);
endmodule
