// Logisim project NSU-FIT-2021-T04L1e05.circ as structural Verilog: 1 circuit, main circuit mycircuit
module mycircuit (
  input  A,
  input  B,
  input  C,
  output R
);

  wire not_1_out, not_2_out, not_3_out, or_2_out;

  not not_1 (not_1_out, C);
  not not_2 (not_2_out, A);
  not not_3 (not_3_out, B);
  or or_1 (R, not_2_out, or_2_out);
  or or_2 (or_2_out, not_3_out, not_1_out);
endmodule
