// Logisim project NSU-FIT-2021-T04L1e07.circ as structural Verilog: 1 circuit, main circuit mycircuit
module mycircuit (
  input  A,
  input  B,
  input  C,
  output R
);

  wire xnor_1_out, xnor_2_out;

  xnor xnor_1 (xnor_1_out, C, A);
  xnor xnor_2 (xnor_2_out, B, C);
  xor xor_1 (R, xnor_2_out, xnor_1_out);
endmodule
