// Logisim project NSU-FIT-2021-T04L1e07_2.circ as structural Verilog: 1 circuit, main circuit mycircuit
module mycircuit (
  input  A,
  input  B,
  input  C,
  output R
);

  wire xnor_1_out;

  xnor xnor_1 (xnor_1_out, C, A);
  xor xor_1 (R, B, xnor_1_out);
endmodule
