// Logisim project NSU-FIT-2021-T04L1e08.circ as structural Verilog: 1 circuit, main circuit mycircuit
module mycircuit (
  input  A,
  input  B,
  input  C,
  output R
);

  wire and_1_out, and_2_out, and_3_out;

  and and_1 (and_1_out, C, B);
  and and_2 (and_2_out, A, B);
  and and_3 (and_3_out, A, C);
  or or_1 (R, and_2_out, and_3_out, and_1_out);
endmodule
