// Logisim project NSU-FIT-2021-T04L1e09.circ as structural Verilog: 1 circuit, main circuit mycircuit
module mycircuit (
  input  A,
  input  B,
  input  C,
  output R
);

  wire not_1_out;

  not not_1 (not_1_out, C);
  and and_1 (R, not_1_out, A);
endmodule
