// Logisim project NSU-FIT-2021-T04L1e15 (1).circ as structural Verilog: 1 circuit, main circuit mycircuit
module mycircuit (
  input  A,
  input  B,
  input  C,
  output R
);

  and and_1 (R, A, B);
endmodule
