// Logisim project NSU-FIT-2021-T04L1e17.circ as structural Verilog: 1 circuit, main circuit mycircuit
module mycircuit (
  input  A,
  input  B,
  input  C,
  output R
);

  wire not_1_out, or_1_out, or_2_out;

  not not_1 (not_1_out, A);
  or or_1 (or_1_out, A, B);
  or or_2 (or_2_out, not_1_out, C);
  and and_1 (R, or_1_out, or_2_out);
endmodule
