// Logisim project NSU-FIT-2021-T04L2e02.circ as structural Verilog: 1 circuit, main circuit formula
module formula (
  input  A,
  input  B,
  input  C,
  output R
);

  wire transistor_1_out, transistor_3_out, transistor_5_out, transistor_7_out;

  Transistor transistor_1 (.in(1'b1), .out(transistor_1_out), .gate(A));
  Transistor #(.\type ("n")) transistor_2 (.in(1'b0), .out(transistor_1_out), .gate(A));
  Transistor #(.\type ("n")) transistor_3 (.in(1'b0), .out(transistor_3_out), .gate(B));
  Transistor #(.\type ("n")) transistor_4 (.in(1'b0), .out(transistor_3_out), .gate(C));
  Transistor transistor_5 (.in(1'b1), .out(transistor_5_out), .gate(B));
  Transistor transistor_6 (.in(transistor_5_out), .out(transistor_3_out), .gate(C));
  Transistor transistor_7 (.in(1'b0), .out(transistor_7_out), .gate(transistor_3_out));
  Transistor transistor_8 (.in(transistor_7_out), .out(R), .gate(transistor_1_out));
  Transistor #(.\type ("n")) transistor_9 (.in(1'b1), .out(R), .gate(transistor_3_out));
  Transistor #(.\type ("n")) transistor_10 (.in(1'b1), .out(R), .gate(transistor_1_out));
endmodule
